# Fritzing sketch RTOS+two_Servo (saved by Fritzing 0.9.6b)

parts:
  J1 = Basic Servo
  M1 = STM32F103C8T6 blue mini board
  J2 = Basic Servo

nets:
  GND: J1.gnd, M1.G, J2.gnd
  VCC: J1.vcc, M1.5V, J2.vcc
  N1: J1.pulse, M1.A1
  N2: M1.A0, J2.pulse
