# Fritzing sketch Uart_controlled_Servo (saved by Fritzing 0.9.6b)

parts:
  J1 = Basic Servo
  M1 = STM32F103C8T6 blue mini board
  Part1 = FTDI Basic Programmer

nets:
  GND: J1.gnd, M1.G, M1.GND, Part1.GND
  VCC: J1.vcc, M1.5V
  N1: J1.pulse, M1.A0
  N2: M1.A9, Part1.RXI
  N3: M1.A10, Part1.TXO
